// Digital circuit main.dig as structural Verilog
module main (
);

  wire ADDR_RS0_A, ADDR_RS0_B, ADDR_RS0_C, ADDR_RS0_D, ADDR_RS1_A, ADDR_RS1_B, ADDR_RS1_C, ADDR_RS1_D,
       alu_1_p1, ALU_A_IN_A, ALU_A_IN_B, ALU_B_IN_A, ALU_B_IN_B, ALU_C_IN_A, ALU_C_IN_B, ALU_D_IN_A,
       ALU_D_IN_B, driver_1_out, imm8, imm16, instruction_decoder_1_p2, instruction_decoder_1_p3,
       instruction_decoder_1_p8, instruction_decoder_1_p11, instruction_decoder_1_p16,
       instruction_decoder_1_p17, nand_1_out, ooo, undriven, undriven_2, undriven_3;
  wire [1:0] ll, rs1;
  wire [2:0] rs0, vvv;
  wire [3:0] Flag_q;
  wire [7:0] A_q, ACC_q, B_q, C_q, D_q, driver_2_out, driver_14_out, driver_15_out, instruction_decoder_1_p7,
       instruction_decoder_1_p10, IR0_q;
  wire [15:0] driver_4_out;

  Driver driver_1 (.in(driver_4_out[0]), .out(driver_1_out));  // open: en
  Register #(.Bits(8)) IR0 (.D(driver_2_out), .C(instruction_decoder_1_p2), .en(instruction_decoder_1_p3), .Q(IR0_q));
  Register #(.Bits(8)) A (.Q(A_q));  // open: D, C, en
  Register #(.Bits(8)) B (.Q(B_q));  // open: D, C, en
  Register #(.Bits(8)) C (.Q(C_q));  // open: D, C, en
  Register #(.Bits(8)) D (.Q(D_q));  // open: D, C, en
  Register #(.Bits(4)) Flag (.Q(Flag_q));  // open: D, C, en
  assign driver_2_out = undriven_3 ? A_q : 8'bz;  // Driver driver_2
  assign driver_4_out[7:0] = ADDR_RS1_A ? A_q : 8'bz;  // Driver driver_3
  assign driver_4_out[15:8] = ADDR_RS0_A ? A_q : 8'bz;  // Driver driver_4
  assign driver_2_out = undriven_2 ? B_q : 8'bz;  // Driver driver_5
  assign driver_4_out[7:0] = ADDR_RS1_B ? B_q : 8'bz;  // Driver driver_6
  assign driver_4_out[15:8] = ADDR_RS0_B ? B_q : 8'bz;  // Driver driver_7
  assign driver_2_out = undriven ? C_q : 8'bz;  // Driver driver_8
  assign driver_4_out[7:0] = ADDR_RS1_C ? C_q : 8'bz;  // Driver driver_9
  assign driver_4_out[15:8] = ADDR_RS0_C ? C_q : 8'bz;  // Driver driver_10
  assign driver_2_out = alu_1_p1 ? D_q : 8'bz;  // Driver driver_11
  assign driver_4_out[7:0] = ADDR_RS1_D ? D_q : 8'bz;  // Driver driver_12
  assign driver_4_out[15:8] = ADDR_RS0_D ? D_q : 8'bz;  // Driver driver_13
  // instruction_decoder instruction_decoder_1: pin names not known; wires that end beside it: driver_1_out, instruction_decoder_1_p2, instruction_decoder_1_p3, ll, IR0_q, ooo, instruction_decoder_1_p7, instruction_decoder_1_p8, vvv, instruction_decoder_1_p10, instruction_decoder_1_p11, imm8, rs0, rs1, imm16, instruction_decoder_1_p16, instruction_decoder_1_p17
  Register #(.Bits(8)) IR1 (
    .D(driver_2_out), .C(instruction_decoder_1_p8), .en(instruction_decoder_1_p11),
    .Q(instruction_decoder_1_p7));
  assign driver_14_out = ALU_A_IN_B ? A_q : 8'bz;  // Driver driver_14
  assign driver_15_out = ALU_A_IN_A ? A_q : 8'bz;  // Driver driver_15
  assign driver_14_out = ALU_B_IN_B ? B_q : 8'bz;  // Driver driver_16
  assign driver_15_out = ALU_B_IN_A ? B_q : 8'bz;  // Driver driver_17
  assign driver_14_out = ALU_C_IN_B ? C_q : 8'bz;  // Driver driver_18
  assign driver_15_out = ALU_C_IN_A ? C_q : 8'bz;  // Driver driver_19
  assign driver_14_out = ALU_D_IN_B ? D_q : 8'bz;  // Driver driver_20
  assign driver_15_out = ALU_D_IN_A ? D_q : 8'bz;  // Driver driver_21
  Register #(.Bits(8)) IR2 (
    .D(driver_2_out), .C(instruction_decoder_1_p16), .en(instruction_decoder_1_p17),
    .Q(instruction_decoder_1_p10));
  Driver driver_22 (.in(imm8), .out(driver_14_out[0]));  // open: en
  // alu alu_1: pin names not known; wires that end beside it: alu_1_p1, Flag_q, driver_14_out, driver_15_out
  nand nand_1 (nand_1_out, ll[0], ll[1]);
  assign driver_15_out = nand_1_out ? ACC_q : 8'bz;  // Driver driver_23
  Driver #(.Bits(8)) driver_24 (.in(ACC_q), .out(driver_2_out));  // open: en
  Decoder #(.Selector_Bits(2)) decoder_1 (
    .sel(vvv[1:0]), .out_0(ALU_A_IN_B), .out_1(ALU_B_IN_B), .out_2(ALU_C_IN_B), .out_3(ALU_D_IN_B));
  Decoder #(.Selector_Bits(2)) decoder_2 (
    .sel(rs0[1:0]), .out_0(ALU_A_IN_A), .out_1(ALU_B_IN_A), .out_2(ALU_C_IN_A), .out_3(ALU_D_IN_A));
  Register #(.Bits(8)) ACC (.Q(ACC_q));  // open: D, C, en
  Decoder #(.Selector_Bits(2)) decoder_3 (
    .sel(rs0[1:0]), .out_0(ADDR_RS0_A), .out_1(ADDR_RS0_B), .out_2(ADDR_RS0_C), .out_3(ADDR_RS0_D));
  Decoder #(.Selector_Bits(2)) decoder_4 (
    .sel(rs1), .out_0(ADDR_RS1_A), .out_1(ADDR_RS1_B), .out_2(ADDR_RS1_C), .out_3(ADDR_RS1_D));
  // Pins of 1 and 8 bits meet at driver_14_out
  // Pins of 1 and 16 bits meet at driver_4_out
  // Pins of 2 and 3 bits meet at rs0

  // Notes on the sheet:
  //   DBUS
  //   ABUS
  //   Registers
  //   Instruction Register
  //   Flag register
  //   Decoder
  //   ALU
  //   ALU Decoders
  //   ACC
  //   Address Decoders
endmodule
